# Fritzing sketch VoltageDividerSchematic (saved by Fritzing 1.0.5)
breadboards: 1

parts:
  BS250_P_Kanal_Mosfet_TO92 = MOSFET-NCHANNEL [package=to-92]
  U1 = LIPO-110mAh [package=lipo-110]
  100k = Resistor [tolerance=±5% resistance=100k package="0603 [SMD]"]
  100k1 = Resistor [tolerance=±5% resistance=100k package="0603 [SMD]"]
  100k2 = Resistor [tolerance=±5% resistance=100k package="0603 [SMD]"]
  U2 = XIAO ESP32C6 [part_number=" XIAO ESP32C6"]
  100nF = Capacitor [package=cap-pth-small2]
  BS250_P_Kanal_Mosfet_TO93 = MOSFET-NCHANNEL [package=to-92]  # not connected
  Filtering = Capacitor [package=cap-pth-small2]  # not connected
  100k3 = Resistor [tolerance=±5% resistance=100k package="0603 [SMD]"]  # not connected

nets:
  N1: BS250_P_Kanal_Mosfet_TO92.D, 100k1.Pin_1
  N2: BS250_P_Kanal_Mosfet_TO92.S, U1.-, 100k2.Pin_0, 100nF.1
  N3: BS250_P_Kanal_Mosfet_TO92.G, 100k.Pin_0, U2.D9
  N4: U1.+, 100k.Pin_1
  N5: 100k1.Pin_0, 100k2.Pin_1, U2.D0, 100nF.2

notes:
  ADC pin
  On/Off pin
  D/S/G
  LOW = TurnON
  Gate <->lipo+ : Make Sure Gate Closed
  when On/Off pin set HIGH

custom parts:
  XIAO ESP32C6: XIAO ESP32C6 is a cost-effective MCU based on Espressif’s ESP32-C6. This compact MCU excels in Matter-compliant smart home applications with its support for various wireless connectivity (2.4GHz Wi-Fi 6, BLE 5.0, Zigbee, and Thread). Designed with the thumb-size footprint and a single-sided mount of the XIAO Series, it's perfect for space-limited projects. Encrypted on the chip, the XIAO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
